# Fritzing sketch minimal-shrimp-battery (saved by Fritzing 0.8.3b)
circuit board: 16.9333cm x 5.64444cm
breadboards: 1

parts:
  U1 = atmega328 [package=dip]
  R1 = Resistor [tolerance=±5% resistance=10k package=THT]
  XTAL1 = Crystal [frequency="16 MHz" package=THT]
  C2 = Ceramic Capacitor [package="100 mil [THT, multilayer]"]
  C1 = Ceramic Capacitor [package="100 mil [THT, multilayer]"]
  B1 = 3 x AAA Battery Mount

nets:
  N1: U1.RESET, R1.Pin_0
  N2: U1.VCC, U1.AVCC, R1.Pin_1, B1.+
  N3: U1.GND#7, C2.0, C1.0, B1.-
  N4: U1.XLAT1, XTAL1.pin_1, C1.1
  N5: U1.XLAT2, XTAL1.pin_0, C2.1

custom parts:
  Ceramic Capacitor: 22pF multilayer Ceramic Capacitor
  3 x AAA Battery Mount: A 3 x AAA battery pack (4.5 Volts with alkaline batteries)
