# Fritzing sketch minimal-shrimp-blink-battery (saved by Fritzing 0.8.4b)
circuit board: 16.9333cm x 5.64444cm
breadboards: 1

parts:
  U1 = atmega328 [package=dip]
  R1 = Resistor [tolerance=±5% resistance=10k package=THT]
  XTAL1 = Crystal [frequency="16 MHz" package=THT]
  B1 = 3 x AAA Battery Mount
  R2 = Resistor [tolerance=±5% resistance=100 package=THT]
  LED1 = LED - 5mm [color="Red (633nm)" package="5 mm [THT]"]
  C1 = Ceramic Capacitor [package="Disc 5.5mm"]
  C2 = Ceramic Capacitor [package="Disc 5.5mm"]

nets:
  N1: U1.RESET, R1.Pin_0
  N2: U1.VCC, U1.AVCC, R1.Pin_1, B1.+
  N3: U1.GND#7, B1.-, C1.0, C2.0
  N4: U1.XLAT1, XTAL1.pin_1, C1.1
  N5: U1.XLAT2, XTAL1.pin_0, C2.1
  N6: U1.D13, LED1.anode
  N7: U1.GND#21, R2.Pin_0
  N8: R2.Pin_1, LED1.cathode

custom parts:
  3 x AAA Battery Mount: A 3 x AAA battery pack (4.5 Volts with alkaline batteries)
  Ceramic Capacitor: 100 nF multilayer Ceramic Capacitor in 5.5mm disc orange packaging
