# Fritzing sketch minimal-shrimp-no-uart (saved by Fritzing 0.8.3b)
circuit board: 16.9333cm x 5.64444cm
breadboards: 1

parts:
  U1 = atmega328 [package=dip]
  R1 = Resistor [tolerance=±5% resistance=10k package=THT]
  XTAL1 = Crystal [frequency="16 MHz" package=THT]
  C3 = Ceramic Capacitor [package="100 mil [THT, multilayer]"]
  C2 = Ceramic Capacitor [package="100 mil [THT, multilayer]"]
  C1 = Ceramic Capacitor [package="100 mil [THT, multilayer]"]
  DTR = male pin header, 1 pin [form="♂ (male)"]
  GND = male pin header, 1 pin [form="♂ (male)"]
  Rx = male pin header, 1 pin [form="♂ (male)"]
  Vcc = male pin header, 1 pin [form="♂ (male)"]
  Tx = male pin header, 1 pin [form="♂ (male)"]

nets:
  N1: U1.RESET, R1.Pin_0, C1.1
  N2: U1.D0_(RX), Rx.pin1
  N3: U1.D1_(TX), Tx.pin1
  N4: U1.VCC, U1.AVCC, R1.Pin_1, Vcc.pin1
  N5: U1.GND#7, C3.0, C2.0, GND.pin1
  N6: U1.XLAT1, XTAL1.pin_1, C2.1
  N7: U1.XLAT2, XTAL1.pin_0, C3.1
  N8: C1.0, DTR.pin1

custom parts:
  Ceramic Capacitor: 22pF multilayer Ceramic Capacitor
  Ceramic Capacitor: 100 nF multilayer Ceramic Capacitor
