# Fritzing sketch minimal-shrimp-pov-battery (saved by Fritzing 0.8.4b)
circuit board: 16.9333cm x 5.64444cm
breadboards: 1

parts:
  U1 = atmega328 [package=dip]
  R1 = Resistor [tolerance=±5% resistance=10k package=THT]
  XTAL1 = Crystal [frequency="16 MHz" package=THT]
  LED1 = LED - 5mm [color="White (4500K)" package="5 mm [THT]"]
  LED2 = LED - 5mm [color="White (4500K)" package="5 mm [THT]"]
  LED3 = LED - 5mm [color="White (4500K)" package="5 mm [THT]"]
  LED4 = LED - 5mm [color="White (4500K)" package="5 mm [THT]"]
  LED5 = LED - 5mm [color="White (4500K)" package="5 mm [THT]"]
  LED6 = LED - 5mm [color="White (4500K)" package="5 mm [THT]"]
  LED7 = LED - 5mm [color="White (4500K)" package="5 mm [THT]"]
  LED8 = LED - 5mm [color="White (4500K)" package="5 mm [THT]"]
  B1 = 3 x AAA Battery Mount
  C1 = Ceramic Capacitor [package="Disc 5.5mm"]
  C2 = Ceramic Capacitor [package="Disc 5.5mm"]

nets:
  N1: U1.RESET, R1.Pin_0
  N2: U1.VCC, U1.AVCC, R1.Pin_1, B1.+
  N3: U1.GND#7, LED1.cathode, LED2.cathode, LED3.cathode, LED4.cathode, LED5.cathode, LED6.cathode, LED7.cathode, LED8.cathode, B1.-, C1.0, C2.0
  N4: U1.XLAT1, XTAL1.pin_1, C1.1
  N5: U1.XLAT2, XTAL1.pin_0, C2.1
  N6: U1.D9_(PWM), LED8.anode
  N7: U1.D10_(PWM), LED7.anode
  N8: U1.D11_(PWM), LED6.anode
  N9: U1.D12, LED5.anode
  N10: U1.A1, LED4.anode
  N11: U1.A2, LED3.anode
  N12: U1.A3, LED2.anode
  N13: U1.A4, LED1.anode

custom parts:
  3 x AAA Battery Mount: A 3 x AAA battery pack (4.5 Volts with alkaline batteries)
  Ceramic Capacitor: 100 nF multilayer Ceramic Capacitor in 5.5mm disc orange packaging
