# Fritzing sketch minimal-shrimp-pov-resistor (saved by Fritzing 0.8.3b)
circuit board: 16.9333cm x 5.64444cm
breadboards: 1

parts:
  U1 = atmega328 [package=dip]
  R1 = Resistor [tolerance=±5% resistance=10k package=THT]
  XTAL1 = Crystal [frequency="16 MHz" package=THT]
  U2 = Embecosm USB to UART [chip_label=USB package="SIP (Single Inline) [THT]"]
  C2 = Ceramic Capacitor [package="100 mil [THT, multilayer]"]
  C3 = Ceramic Capacitor [package="100 mil [THT, multilayer]"]
  C1 = Ceramic Capacitor [package="100 mil [THT, multilayer]"]
  LED1 = LED - 5mm [color="Red (633nm)" package="5 mm [THT]"]
  LED2 = LED - 5mm [color="Red (633nm)" package="5 mm [THT]"]
  LED3 = LED - 5mm [color="Red (633nm)" package="5 mm [THT]"]
  LED4 = LED - 5mm [color="Red (633nm)" package="5 mm [THT]"]
  LED5 = LED - 5mm [color="Red (633nm)" package="5 mm [THT]"]
  LED6 = LED - 5mm [color="Red (633nm)" package="5 mm [THT]"]
  LED7 = LED - 5mm [color="Red (633nm)" package="5 mm [THT]"]
  LED8 = LED - 5mm [color="Red (633nm)" package="5 mm [THT]"]
  R2 = Resistor [tolerance=±5% resistance=100 package=THT]
  R6 = Resistor [tolerance=±5% resistance=100 package=THT]
  R3 = Resistor [tolerance=±5% resistance=100 package=THT]
  R4 = Resistor [tolerance=±5% resistance=100 package=THT]
  R5 = Resistor [tolerance=±5% resistance=100 package=THT]
  R9 = Resistor [tolerance=±5% resistance=100 package=THT]
  R8 = Resistor [tolerance=±5% resistance=100 package=THT]
  R7 = Resistor [tolerance=±5% resistance=100 package=THT]

nets:
  N1: U1.RESET, R1.Pin_0, C1.1
  N2: U1.D0_(RX), U2.TXD
  N3: U1.D1_(TX), U2.RXD
  VCC: U1.VCC, U1.AVCC, R1.Pin_1, U2.VCC
  N4: U1.GND#7, U2.GND, C2.0, C3.0, LED1.cathode, LED2.cathode, LED3.cathode, LED4.cathode, LED5.cathode, LED6.cathode, LED7.cathode, LED8.cathode
  N5: U1.XLAT1, XTAL1.pin_1, C3.1
  N6: U1.XLAT2, XTAL1.pin_0, C2.1
  N7: U1.D9_(PWM), R9.Pin_0
  N8: U1.D10_(PWM), R8.Pin_0
  N9: U1.D11_(PWM), R7.Pin_0
  N10: U1.D12, R6.Pin_0
  N11: U1.A1, R5.Pin_0
  N12: U1.A2, R4.Pin_0
  N13: U1.A3, R3.Pin_0
  N14: U1.A4, R2.Pin_0
  N15: U2.DTR, C1.0
  N16: LED1.anode, R2.Pin_1
  N17: LED2.anode, R3.Pin_1
  N18: LED3.anode, R4.Pin_1
  N19: LED4.anode, R5.Pin_1
  N20: LED5.anode, R6.Pin_1
  N21: LED6.anode, R7.Pin_1
  N22: LED7.anode, R8.Pin_1
  N23: LED8.anode, R9.Pin_1

custom parts:
  Embecosm USB to UART: The Embecosm USB to UART serial port for use with Arduino like devices. 6 inline pins on 0.1in spacing.
  Ceramic Capacitor: 22pF multilayer Ceramic Capacitor
  Ceramic Capacitor: 100 nF multilayer Ceramic Capacitor
