# Fritzing sketch minimal-shrimp (saved by Fritzing 0.8.3b)
circuit board: 16.9333cm x 5.64444cm
breadboards: 1

parts:
  U1 = atmega328 [package=dip]
  C1 = Ceramic Capacitor [package="100 mil [THT, multilayer]"]
  C3 = Ceramic Capacitor [package="100 mil [THT, multilayer]"]
  R1 = Resistor [tolerance=±5% resistance=10k package=THT]
  XTAL1 = Crystal [frequency="16 MHz" package=THT]
  C9 = Ceramic Capacitor [package="100 mil [THT, multilayer]"]
  U2 = Embecosm USB to UART [chip_label=USB package="SIP (Single Inline) [THT]"]

nets:
  N1: U1.RESET, C1.1, R1.Pin_0
  N2: U1.D0_(RX), U2.RXD
  N3: U1.D1_(TX), U2.TXD
  VCC: U1.VCC, U1.AVCC, R1.Pin_1, U2.VCC
  GND: U1.GND, C3.0, C9.0, U2.GND
  N4: U1.XLAT1, C3.1, XTAL1.pin_1
  N5: U1.XLAT2, XTAL1.pin_0, C9.1
  N6: C1.0, U2.DTR

custom parts:
  Ceramic Capacitor: 100 nF multilayer Ceramic Capacitor
  Ceramic Capacitor: 100 nF multilayer Ceramic Capacitor
  Embecosm USB to UART: The Embecosm USB to UART serial port for use with Arduino like devices. 6 inline pins on 0.1in spacing.
