# Fritzing sketch protected-shrimp-battery (saved by Fritzing 0.8.3b)
circuit board: 16.9333cm x 5.64444cm
breadboards: 1

parts:
  U1 = atmega328 [package=dip]
  C1 = Ceramic Capacitor [package="100 mil [THT, multilayer]"]
  C2 = Ceramic Capacitor [package="100 mil [THT, multilayer]"]
  S1 = Pushbutton [package="[THT]"]
  R1 = Resistor [tolerance=±5% resistance=10k package=THT]
  D1 = Rectifier Diode [part_number=1N4001 package="300 mil [THT]"]
  XTAL1 = Crystal [frequency="16 MHz" package=THT]
  C8 = Electrolytic Capacitor [package="100 mil [THT, electrolytic]"]
  VCC2 = 3 x AAA Battery Mount
  C9 = Ceramic Capacitor [package="100 mil [THT, multilayer]"]
  C10 = Ceramic Capacitor [package="100 mil [THT, multilayer]"]
  C11 = Ceramic Capacitor [package="100 mil [THT, multilayer]"]
  C12 = Ceramic Capacitor [package="100 mil [THT, multilayer]"]

nets:
  N1: U1.RESET, U1.GND, C1.1, C2.1, S1.Pin_1, S1.Pin_2, S1.Pin_3, S1.Pin_4, R1.Pin_0, D1.anode, C8.-, VCC2.-, C9.0, C10.0, C11.0, C12.0
  N2: U1.VCC, U1.AVCC, C2.0, R1.Pin_1, D1.cathode, C8.+, VCC2.+, C12.1
  N3: U1.XLAT1, XTAL1.pin_1, C9.1
  N4: U1.XLAT2, XTAL1.pin_0, C10.1
  N5: U1.AREF, C11.1

custom parts:
  Ceramic Capacitor: 100 nF multilayer Ceramic Capacitor
  Pushbutton: A generic pushbutton.
  Electrolytic Capacitor: A small electrolytic capacitor
  3 x AAA Battery Mount: A 3 x AAA battery pack (4.5 Volts with alkaline batteries)
  Ceramic Capacitor: 22pF multilayer Ceramic Capacitor
  Ceramic Capacitor: 100 nF multilayer Ceramic Capacitor
