# Fritzing sketch protected-shrimp-pov-resistor (saved by Fritzing 0.8.3b)
circuit board: 16.9333cm x 5.64444cm
breadboards: 1

parts:
  U1 = atmega328 [package=dip]
  U2 = SIP - 6 pins [chip_label=IC package="SIP (Single Inline) [THT]"]
  C1 = Ceramic Capacitor [package="100 mil [THT, multilayer]"]
  S1 = Pushbutton [package="[THT]"]
  R1 = Resistor [tolerance=±5% resistance=10k package=THT]
  D1 = Rectifier Diode [part_number=1N4001 package="300 mil [THT]"]
  XTAL1 = Crystal [frequency="16 MHz" package=THT]
  C8 = Electrolytic Capacitor [package="100 mil [THT, electrolytic]"]
  LED1 = LED - 5mm [color="Red (633nm)" package="5 mm [THT]"]
  LED2 = LED - 5mm [color="Red (633nm)" package="5 mm [THT]"]
  LED3 = LED - 5mm [color="Red (633nm)" package="5 mm [THT]"]
  LED4 = LED - 5mm [color="Red (633nm)" package="5 mm [THT]"]
  LED5 = LED - 5mm [color="Red (633nm)" package="5 mm [THT]"]
  LED6 = LED - 5mm [color="Red (633nm)" package="5 mm [THT]"]
  LED7 = LED - 5mm [color="Red (633nm)" package="5 mm [THT]"]
  LED8 = LED - 5mm [color="Red (633nm)" package="5 mm [THT]"]
  R2 = Resistor [tolerance=±5% resistance=100 package=THT]
  R3 = Resistor [tolerance=±5% resistance=100 package=THT]
  R4 = Resistor [tolerance=±5% resistance=100 package=THT]
  R5 = Resistor [tolerance=±5% resistance=100 package=THT]
  R6 = Resistor [tolerance=±5% resistance=100 package=THT]
  R7 = Resistor [tolerance=±5% resistance=100 package=THT]
  R8 = Resistor [tolerance=±5% resistance=100 package=THT]
  R9 = Resistor [tolerance=±5% resistance=100 package=THT]
  C9 = Ceramic Capacitor [package="100 mil [THT, multilayer]"]
  C11 = Ceramic Capacitor [package="100 mil [THT, multilayer]"]
  C12 = Ceramic Capacitor [package="100 mil [THT, multilayer]"]
  C13 = Ceramic Capacitor [package="100 mil [THT, multilayer]"]
  C14 = Ceramic Capacitor [package="100 mil [THT, multilayer]"]

nets (from the breadboard view):
  GND: U1.RESET, U1.GND, U2.GND, C1.1, S1.Pin_1, S1.Pin_2, S1.Pin_3, S1.Pin_4, R1.Pin_0, D1.anode, C8.-, C9.1, C11.0, C12.0, C13.0, C14.0
  N1: U1.D0_(RX), U2.TXD
  N2: U1.D1_(TX), U2.RXD
  VCC: U1.VCC, U1.AVCC, U2.VCC, R1.Pin_1, D1.cathode, C8.+, C9.0, C13.1
  N3: U1.XLAT1, XTAL1.pin_1, C11.1
  N4: U1.XLAT2, XTAL1.pin_0, C12.1
  N5: U1.D9_(PWM), R6.Pin_0
  N6: U1.D10_(PWM), R7.Pin_0
  N7: U1.D11_(PWM), R8.Pin_0
  N8: U1.D12, R9.Pin_0
  N9: U1.AREF, C14.1
  N10: U1.A1, R5.Pin_0
  N11: U1.A2, R4.Pin_0
  N12: U1.A3, R3.Pin_0
  N13: U1.A4, R2.Pin_0
  N14: U2.DTR, C1.0
  N15: LED1.cathode, LED2.cathode, LED3.cathode, LED4.cathode, LED5.cathode, LED6.cathode, LED7.cathode, LED8.cathode
  N16: LED1.anode, R2.Pin_1
  N17: LED2.anode, R3.Pin_1
  N18: LED3.anode, R4.Pin_1
  N19: LED4.anode, R5.Pin_1
  N20: LED5.anode, R7.Pin_1
  N21: LED6.anode, R8.Pin_1
  N22: LED7.anode, R6.Pin_1
  N23: LED8.anode, R9.Pin_1

custom parts:
  SIP - 6 pins: A SIP stand-in part for whatever you want. With 6 pins on a 300 mil single inline package (SIP) footprint.
  Ceramic Capacitor: 100 nF multilayer Ceramic Capacitor
  Pushbutton: A generic pushbutton.
  Electrolytic Capacitor: A small electrolytic capacitor
  Ceramic Capacitor: 100 nF multilayer Ceramic Capacitor
  Ceramic Capacitor: 22pF multilayer Ceramic Capacitor
